# Fritzing sketch Schematic (saved by Fritzing 0.9.3b)

parts:
  U1 = ESP32-38PinWide [part_number=ESP32-38PinWide]
  S1 = Pushbutton [package="[THT]"]
  S3 = Pushbutton [package="[THT]"]
  S4 = Pushbutton [package="[THT]"]

nets:
  N1: U1.GPIO16, S1.Pin_3, S1.Pin_4
  N2: U1.GPIO17, S3.Pin_3, S3.Pin_4
  N3: U1.GPIO18, S4.Pin_3, S4.Pin_4
  N4: U1.GND, S1.Pin_1, S3.Pin_1, S3.Pin_2, S4.Pin_1, S4.Pin_2

custom parts:
  ESP32-38PinWide: Generic 38-Pin ESP32 with wide format (only access to one side of pins on a breadboard) based on Stephen Lilley's HiLetgo ESP-WROOM-32 ESP32 ESP-32S Development Board.
